// Logisim project ALU.circ as structural Verilog: 4 circuits, main circuit main
module main (
);

  wire _1_3_out, _1_5_out, _1_out, _2_3_out, _2_5_out, _2_out, _4_3_out, _4_5_out, _4_out, _8_3_out,
       _8_5_out, _8_out, alu_1_p6, alu_1_p7, binary_to_bcd_2_p1, input_only_1__1_2, input_only_1__8_2,
       input_only_1_out_11, input_only_1_out_12, input_only_1_request_out, input_only_1_send_2,
       input_only_2__1_2, input_only_2__8_2, input_only_2_out_11, input_only_2_out_12,
       input_only_2_request_out, input_only_2_send_2, input_only_3__1_2, input_only_3__8_2,
       input_only_3_out_11, input_only_3_out_12, input_only_3_request_out, input_only_3_send_2, S_2_out,
       S_3_out, S_out;
  wire [3:0] binary_to_bcd_1_p1, binary_to_bcd_1_p2, binary_to_bcd_1_p3, binary_to_bcd_2_p2,
       binary_to_bcd_2_p3, controlled_buffer_1_out, input_only_1_data, input_only_2_data, input_only_3_data,
       pull_resistor_1_node, pull_resistor_2_node;

  Button _8 (.out(_8_out));
  LED _8_2 (.in(input_only_1__1_2));
  Button _8_3 (.out(_8_3_out));
  LED _8_4 (.in(input_only_2__1_2));
  Button _8_5 (.out(_8_5_out));
  LED _8_6 (.in(input_only_3__1_2));
  Button _2 (.out(_2_out));
  Button _4 (.out(_4_out));
  Button _1 (.out(_1_out));
  LED _1_2 (.in(input_only_1__8_2));
  LED _2_2 (.in(input_only_1_out_12));
  LED _4_2 (.in(input_only_1_out_11));
  Button _1_3 (.out(_1_3_out));
  Button _4_3 (.out(_4_3_out));
  Button _2_3 (.out(_2_3_out));
  LED _2_4 (.in(input_only_2_out_12));
  LED _4_4 (.in(input_only_2_out_11));
  LED _1_4 (.in(input_only_2__8_2));
  Button _1_5 (.out(_1_5_out));
  Button _2_5 (.out(_2_5_out));
  Button _4_5 (.out(_4_5_out));
  LED _2_6 (.in(input_only_3_out_12));
  LED _4_6 (.in(input_only_3_out_11));
  LED _1_6 (.in(input_only_3__8_2));
  Button S (.out(S_out));
  Input_Only input_only_1 (
    .Data(input_only_1_data), .Send_2(input_only_1_send_2), .Send(S_out),
    .Request_Out(input_only_1_request_out), ._1(_8_out), .in_2(_4_out), .in_3(_2_out), ._8(_1_out),
    ._1_2(input_only_1__1_2), .out_11(input_only_1_out_11), .out_12(input_only_1_out_12),
    ._8_2(input_only_1__8_2));  // open: Request_In
  LED R (.in(input_only_1_request_out));
  Button S_2 (.out(S_2_out));
  Input_Only input_only_2 (
    .Data(input_only_2_data), .Send_2(input_only_2_send_2), .Send(S_2_out),
    .Request_Out(input_only_2_request_out), ._1(_8_3_out), .in_2(_4_3_out), .in_3(_2_3_out), ._8(_1_3_out),
    ._1_2(input_only_2__1_2), .out_11(input_only_2_out_11), .out_12(input_only_2_out_12),
    ._8_2(input_only_2__8_2));  // open: Request_In
  LED R_2 (.in(input_only_2_request_out));
  Button S_3 (.out(S_3_out));
  Input_Only input_only_3 (
    .Data(input_only_3_data), .Send_2(input_only_3_send_2), .Send(S_3_out),
    .Request_Out(input_only_3_request_out), ._1(_8_5_out), .in_2(_4_5_out), .in_3(_2_5_out), ._8(_1_5_out),
    ._1_2(input_only_3__1_2), .out_11(input_only_3_out_11), .out_12(input_only_3_out_12),
    ._8_2(input_only_3__8_2));  // open: Request_In
  LED R_3 (.in(input_only_3_request_out));
  assign controlled_buffer_1_out = input_only_1_send_2 ? input_only_1_data : 4'bz;  // Controlled_Buffer controlled_buffer_1
  Pull_Resistor pull_resistor_1 (.node(pull_resistor_1_node));
  Pull_Resistor pull_resistor_2 (.node(pull_resistor_2_node));
  Pull_Resistor pull_resistor_3 (.node(controlled_buffer_1_out));
  assign pull_resistor_2_node = input_only_2_send_2 ? input_only_2_data : 4'bz;  // Controlled_Buffer controlled_buffer_2
  assign pull_resistor_1_node = input_only_3_send_2 ? input_only_3_data : 4'bz;  // Controlled_Buffer controlled_buffer_3
  // Binary_to_BCD binary_to_bcd_1: pin names not known; wires that end beside it: binary_to_bcd_1_p1, binary_to_bcd_1_p2, binary_to_bcd_1_p3
  assign binary_to_bcd_1_p1 = controlled_buffer_1_out | pull_resistor_2_node | pull_resistor_1_node;  // OR_Gate or_1, 4 bits wide
  Hex_Digit_Display hex_digit_display_1 (.value(binary_to_bcd_1_p3));  // open: dp
  Hex_Digit_Display hex_digit_display_2 (.value(binary_to_bcd_1_p2));  // open: dp
  // Binary_to_BCD binary_to_bcd_2: pin names not known; wires that end beside it: binary_to_bcd_2_p1, binary_to_bcd_2_p2, binary_to_bcd_2_p3
  // ALU alu_1: pin names not known; wires that end beside it: binary_to_bcd_1_p1, input_only_1_send_2, input_only_2_send_2, input_only_3_send_2, binary_to_bcd_2_p1, alu_1_p6, alu_1_p7
  Hex_Digit_Display hex_digit_display_3 (.value(binary_to_bcd_2_p2));  // open: dp
  Hex_Digit_Display hex_digit_display_4 (.value(binary_to_bcd_2_p3));  // open: dp
  // Square_LED Overflow: pin names not known; wires that end beside it: alu_1_p6
  // Square_LED Flag: pin names not known; wires that end beside it: alu_1_p7

  // Notes on the sheet:
  //   Binary to binary coded decimal
endmodule

module ALU (
  input  [3:0] Data,
  input  Set_A,
  input  Set_B,
  input  Set_O,
  input  Reset,
  input  [2:0] Flags,
  output [3:0] Output,
  output Overflow,
  output Flag
);

  wire comparator_1_eq, comparator_1_gt, comparator_1_lt, not_3_out, or_2_out, or_3_out;
  wire [3:0] adder_1_out, AND_out, multiplier_1_cout, multiplier_1_out, not_1_out, not_2_out, OR_out,
       register_1_q, register_2_q, register_3_q, shifter_1_out, shifter_2_out, shifter_3_out, shifter_4_out,
       XOR_out;

  Register #(.width(4), .trigger("high")) register_1 (
    .D(Data), .Q(register_1_q), .clk(Set_A), .clr(Reset));  // open: en
  Register #(.width(4), .trigger("high")) register_2 (
    .D(Data), .Q(register_2_q), .clk(Set_B), .clr(Reset));  // open: en
  Register #(.width(4), .trigger("high")) register_3 (
    .D(Data), .Q(register_3_q), .clk(Set_O), .clr(Reset));  // open: en
  Pull_Resistor pull_resistor_1 (.node(register_2_q));
  Pull_Resistor pull_resistor_2 (.node(register_1_q));
  Pull_Resistor pull_resistor_3 (.node(Flags));
  assign not_1_out = ~register_1_q;  // NOT_Gate not_1, 4 bits wide
  assign not_2_out = ~register_2_q;  // NOT_Gate not_2, 4 bits wide
  assign OR_out = register_1_q | register_2_q;  // OR_Gate OR, 4 bits wide
  assign AND_out = register_1_q & register_2_q;  // AND_Gate AND, 4 bits wide
  assign XOR_out = register_1_q ^ register_2_q;  // XOR_Gate XOR, 4 bits wide
  Adder #(.width(4)) adder_1 (.a(register_1_q), .b(register_2_q), .out(adder_1_out), .cout(Overflow));  // open: cin
  Multiplier #(.width(4)) multiplier_1 (
    .a(register_1_q), .b(register_2_q), .out(multiplier_1_out), .cout(multiplier_1_cout));  // open: cin
  Shifter #(.width(4)) shifter_1 (.in(register_1_q), .\dist (register_2_q[1:0]), .out(shifter_1_out));
  Shifter #(.width(4), .shift("lr")) shifter_2 (.in(register_1_q), .\dist (register_2_q[1:0]), .out(shifter_2_out));
  Shifter #(.width(4), .shift("rl")) shifter_3 (.in(register_1_q), .\dist (register_2_q[1:0]), .out(shifter_3_out));
  Shifter #(.width(4), .shift("rr")) shifter_4 (.in(register_2_q), .\dist (register_2_q[1:0]), .out(shifter_4_out));
  Comparator #(.width(4), .mode("unsigned")) comparator_1 (
    .a(register_2_q), .b(register_1_q), .gt(comparator_1_gt), .eq(comparator_1_eq), .lt(comparator_1_lt));
  or or_2 (or_2_out, comparator_1_gt, comparator_1_eq);
  or or_3 (or_3_out, comparator_1_eq, comparator_1_lt);
  not not_3 (not_3_out, comparator_1_eq);
  Multiplexer #(.select(4), .width(4), .enable("false")) multiplexer_1 (
    .in0(register_1_q), .in1(register_2_q), .in2(not_1_out), .in3(not_2_out), .in4(OR_out), .in5(AND_out),
    .in6(XOR_out), .in7(adder_1_out), .in8(multiplier_1_out), .in9(multiplier_1_cout), .in10(shifter_1_out),
    .in11(shifter_2_out), .in12(shifter_3_out), .in13(shifter_4_out), .in14(4'b0000), .in15(4'b1111),
    .out(Output), .sel(register_3_q));
  Multiplexer #(.select(3), .enable("false")) multiplexer_2 (
    .in0(comparator_1_gt), .in1(comparator_1_eq), .in2(comparator_1_lt), .in3(or_2_out), .in4(or_3_out),
    .in5(not_3_out), .in6(1'b0), .in7(1'b1), .out(Flag), .sel(Flags));

  // Notes on the sheet:
  //   Registers to save memory temporarily
  //   MUX is a combinational logic circuit which lets to switch one input line to a single common output line
  //   A
  //   B
  //   C
  //   Adder
endmodule

module Explanations (
  input  A,
  input  B,
  input  [3:0] _8_4_2_1,
  input  A_2,
  input  [3:0] _8_4_2_1_2,
  input  B_2,
  input  Carry_in,
  input  _2,
  input  _1,
  input  _2_2,
  input  _1_2,
  input  _1_3,
  input  _8,
  input  _7,
  input  _6,
  input  _5,
  input  _4,
  input  _3,
  input  _2_3,
  input  _1_4,
  input  Direction,
  input  [7:0] in_22,
  output Carry_out,
  output Sum,
  output [7:0] Output,
  output Carry_out_2,
  output Sum_2,
  output _4_2,
  output _2_4,
  output _1_5,
  output _8_2,
  output _7_2,
  output _6_2,
  output _5_2,
  output _4_3,
  output _3_2,
  output _2_5,
  output _1_6,
  output [7:0] out_39,
  output [7:0] out_40,
  output [7:0] out_41,
  output [7:0] out_42,
  output [7:0] out_43
);

  wire adder_1_cout, adder_2_cout, adder_2_out, adder_3_cout, adder_3_out, adder_4_cout, adder_4_out,
       adder_5_cout, adder_6_cout, adder_6_out, adder_7_cout, adder_7_out, adder_8_cout, adder_8_out,
       adder_9_cout, adder_10_cout, adder_11_cout, and_1_out, and_3_out, and_4_out, and_5_out, and_6_out,
       and_7_out, and_8_out, and_10_out, and_11_out, and_12_out, and_13_out, and_14_out, and_15_out,
       and_16_out, and_17_out, and_18_out, and_19_out, and_20_out, and_23_out, and_24_out, and_25_out,
       and_26_out, and_27_out, and_28_out, and_29_out, and_30_out, and_31_out, and_32_out, and_33_out,
       and_34_out, and_35_out, and_36_out, and_37_out, not_1_out, or_4_out, xor_1_out, xor_2_out, xor_3_out;

  not not_1 (not_1_out, Direction);
  and and_1 (and_1_out, _8, Direction);
  and and_2 (_8_2, not_1_out, _7);
  and and_3 (and_3_out, _7, Direction);
  or or_1 (_7_2, and_1_out, and_8_out);
  and and_4 (and_4_out, A_2, B_2);
  xor xor_1 (xor_1_out, A_2, B_2);
  and and_5 (and_5_out, _1, _1_2);
  xor xor_2 (xor_2_out, _1, _1_2);
  and and_6 (and_6_out, _2, _2_2);
  xor xor_3 (xor_3_out, _2, _2_2);
  and and_7 (and_7_out, _6, Direction);
  and and_8 (and_8_out, not_1_out, _6);
  or or_2 (_6_2, and_3_out, and_13_out);
  and and_9 (Carry_out, A, B);
  xor xor_4 (Sum, A, B);
  and and_10 (and_10_out, xor_2_out, _1_3);
  xor xor_5 (_1_5, xor_2_out, _1_3);
  and and_11 (and_11_out, xor_3_out, or_4_out);
  xor xor_6 (_2_4, xor_3_out, or_4_out);
  and and_12 (and_12_out, _5, Direction);
  and and_13 (and_13_out, not_1_out, _5);
  or or_3 (_5_2, and_7_out, and_16_out);
  Shifter shifter_1 (.in(in_22), .\dist (3'b010), .out(out_39));
  Shifter #(.shift("lr")) shifter_2 (.in(in_22), .\dist (3'b010), .out(out_40));
  Shifter #(.shift("ar")) shifter_3 (.in(in_22), .\dist (3'b010), .out(out_41));
  Shifter #(.shift("rl")) shifter_4 (.in(in_22), .\dist (3'b010), .out(out_42));
  Shifter #(.shift("rr")) shifter_5 (.in(in_22), .\dist (3'b010), .out(out_43));
  xor xor_7 (Carry_out_2, and_4_out, and_14_out);
  and and_14 (and_14_out, xor_1_out, Carry_in);
  xor xor_8 (Sum_2, xor_1_out, Carry_in);
  or or_4 (or_4_out, and_5_out, and_10_out);
  or or_5 (_4_2, and_6_out, and_11_out);
  and and_15 (and_15_out, _4, Direction);
  and and_16 (and_16_out, not_1_out, _4);
  or or_6 (_4_3, and_12_out, and_17_out);
  and and_17 (and_17_out, not_1_out, _3);
  or or_7 (_3_2, and_15_out, and_19_out);
  and and_18 (and_18_out, _3, Direction);
  and and_19 (and_19_out, not_1_out, _2_3);
  or or_8 (_2_5, and_18_out, and_20_out);
  and and_20 (and_20_out, not_1_out, _1_4);
  and and_21 (_1_6, _2_3, Direction);
  and and_22 (Output[0], _8_4_2_1[0], _8_4_2_1_2[0]);
  and and_23 (and_23_out, _8_4_2_1[1], _8_4_2_1_2[0]);
  and and_24 (and_24_out, _8_4_2_1[2], _8_4_2_1_2[0]);
  and and_25 (and_25_out, _8_4_2_1[3], _8_4_2_1_2[0]);
  and and_26 (and_26_out, _8_4_2_1[3], _8_4_2_1_2[1]);
  and and_27 (and_27_out, _8_4_2_1[0], _8_4_2_1_2[1]);
  and and_28 (and_28_out, _8_4_2_1[1], _8_4_2_1_2[1]);
  and and_29 (and_29_out, _8_4_2_1[2], _8_4_2_1_2[1]);
  Adder #(.width(1)) adder_1 (.a(and_23_out), .b(and_27_out), .out(Output[1]), .cin(1'b0), .cout(adder_1_cout));
  Adder #(.width(1)) adder_2 (
    .a(and_24_out), .b(and_28_out), .out(adder_2_out), .cin(adder_1_cout), .cout(adder_2_cout));
  Adder #(.width(1)) adder_3 (
    .a(and_25_out), .b(and_29_out), .out(adder_3_out), .cin(adder_2_cout), .cout(adder_3_cout));
  and and_30 (and_30_out, _8_4_2_1[3], _8_4_2_1_2[2]);
  Adder #(.width(1)) adder_4 (.a(adder_3_cout), .b(and_26_out), .out(adder_4_out), .cin(1'b0), .cout(adder_4_cout));
  and and_31 (and_31_out, _8_4_2_1[0], _8_4_2_1_2[2]);
  and and_32 (and_32_out, _8_4_2_1[1], _8_4_2_1_2[2]);
  and and_33 (and_33_out, _8_4_2_1[2], _8_4_2_1_2[2]);
  and and_34 (and_34_out, _8_4_2_1[3], _8_4_2_1_2[3]);
  Adder #(.width(1)) adder_5 (.a(adder_2_out), .b(and_31_out), .out(Output[2]), .cin(1'b0), .cout(adder_5_cout));
  Adder #(.width(1)) adder_6 (
    .a(adder_3_out), .b(and_32_out), .out(adder_6_out), .cin(adder_5_cout), .cout(adder_6_cout));
  Adder #(.width(1)) adder_7 (
    .a(adder_4_out), .b(and_33_out), .out(adder_7_out), .cin(adder_6_cout), .cout(adder_7_cout));
  Adder #(.width(1)) adder_8 (
    .a(adder_4_cout), .b(and_30_out), .out(adder_8_out), .cin(adder_7_cout), .cout(adder_8_cout));
  Adder #(.width(1)) adder_9 (.a(adder_6_out), .b(and_35_out), .out(Output[3]), .cin(1'b0), .cout(adder_9_cout));
  and and_35 (and_35_out, _8_4_2_1[0], _8_4_2_1_2[3]);
  Adder #(.width(1)) adder_10 (
    .a(adder_7_out), .b(and_36_out), .out(Output[4]), .cin(adder_9_cout), .cout(adder_10_cout));
  and and_36 (and_36_out, _8_4_2_1[1], _8_4_2_1_2[3]);
  Adder #(.width(1)) adder_11 (
    .a(adder_8_out), .b(and_37_out), .out(Output[5]), .cin(adder_10_cout), .cout(adder_11_cout));
  and and_37 (and_37_out, _8_4_2_1[2], _8_4_2_1_2[3]);
  Adder #(.width(1)) adder_12 (
    .a(adder_8_cout), .b(and_34_out), .out(Output[6]), .cin(adder_11_cout), .cout(Output[7]));

  // Other names for the same wires on the sheet: X0 = _8_4_2_1[0]; X1 = _8_4_2_1[1]; X2 = _8_4_2_1[2];
  //   X3 = _8_4_2_1[3]; Y0 = _8_4_2_1_2[0]; Y1 = _8_4_2_1_2[1]; Y2 = _8_4_2_1_2[2]; Y3 = _8_4_2_1_2[3]

  // Notes on the sheet:
  //   AND
  //   XOR
  //   Half adders are need when adding 1 bit numbers (0,1)
  //   AND
  //   XOR
  //   Adders are need when adding even more numbers
  //   XOR
  //   Shifters
  //   Multiplier
  //   128 64 32 16 8 4 2 1
endmodule

// IU
module Input_Only (
  input  _1,
  input  in_2,
  input  in_3,
  input  _8,
  input  Send,
  input  Request_In,
  output [3:0] Data,
  output Send_2,
  output Request_Out,
  output _1_2,
  output out_11,
  output out_12,
  output _8_2
);

  T_Flip_Flop t_ff_1 (.clk(_1), .T(_1), .Q(_1_2));  // open: Qn, preset, reset, en
  T_Flip_Flop t_ff_2 (.clk(in_2), .T(in_2), .Q(Data[2]));  // open: Qn, preset, reset, en
  T_Flip_Flop t_ff_3 (.clk(in_3), .T(in_3), .Q(Data[1]));  // open: Qn, preset, reset, en
  T_Flip_Flop t_ff_4 (.clk(_8), .T(_8), .Q(_8_2));  // open: Qn, preset, reset, en

  assign {Data[3], Data[0]} = {_1_2, _8_2};
  assign out_11 = Data[2];
  assign out_12 = Data[1];
  assign Request_Out = Request_In;
  assign Send_2 = Send;
endmodule
